// Logisim project Most beutiful-1.circ as structural Verilog
module main (
  input  B,
  input  in_2,
  input  in_3,
  input  in_4,
  input  in_5,
  input  in_6,
  input  in_7,
  input  in_8,
  input  [3:0] SLOT_B,
  input  [3:0] SLOT_A,
  input  B_2,
  input  in_12,
  input  in_13,
  input  in_14,
  output out_15,
  output out_16,
  output out_17,
  output out_18
);

  wire and_1_out, and_2_out, and_3_out, and_6_out, comparator_1_eq, comparator_1_gt, comparator_1_lt,
       d_ff_1_q, d_ff_2_q, d_ff_3_q, d_ff_4_q, d_ff_5_q, d_ff_6_q, d_ff_7_q, d_ff_8_q, not_1_out, or_1_out,
       or_2_out, xnor_1_out, xnor_2_out, xnor_3_out, xnor_4_out, xnor_5_out, xnor_6_out, xnor_7_out,
       xnor_8_out, xor_1_out;

  D_Flip_Flop #(.trigger("high")) d_ff_1 (.clk(or_1_out), .D(in_5), .Q(d_ff_1_q));  // open: Qn, preset, en, reset
  D_Flip_Flop #(.trigger("high")) d_ff_2 (.clk(or_1_out), .D(in_6), .Q(d_ff_2_q));  // open: Qn, preset, en, reset
  D_Flip_Flop #(.trigger("high")) d_ff_3 (.clk(or_1_out), .D(in_7), .Q(d_ff_3_q));  // open: Qn, preset, en, reset
  D_Flip_Flop #(.trigger("high")) d_ff_4 (.clk(or_1_out), .D(in_8), .Q(d_ff_4_q));  // open: Qn, preset, en, reset
  D_Flip_Flop #(.trigger("high")) d_ff_5 (.clk(or_2_out), .D(in_5), .Q(d_ff_5_q));  // open: Qn, preset, en, reset
  D_Flip_Flop #(.trigger("high")) d_ff_6 (.clk(or_2_out), .D(in_6), .Q(d_ff_6_q));  // open: Qn, preset, en, reset
  D_Flip_Flop #(.trigger("high")) d_ff_7 (.clk(or_2_out), .D(in_7), .Q(d_ff_7_q));  // open: Qn, preset, en, reset
  D_Flip_Flop #(.trigger("high")) d_ff_8 (.clk(or_2_out), .D(in_8), .Q(d_ff_8_q));  // open: Qn, preset, en, reset
  xnor xnor_1 (xnor_1_out, d_ff_1_q, in_2);
  xnor xnor_2 (xnor_2_out, d_ff_2_q, B);
  xnor xnor_3 (xnor_3_out, in_3, d_ff_3_q);
  xnor xnor_4 (xnor_4_out, in_4, d_ff_4_q);
  xnor xnor_5 (xnor_5_out, d_ff_5_q, in_12);
  xnor xnor_6 (xnor_6_out, d_ff_6_q, B_2);
  xnor xnor_7 (xnor_7_out, in_13, d_ff_7_q);
  xnor xnor_8 (xnor_8_out, in_14, d_ff_8_q);
  and and_1 (and_1_out, xnor_1_out, xnor_2_out, xnor_3_out, xnor_4_out);
  and and_2 (and_2_out, xnor_5_out, xnor_6_out, xnor_7_out, xnor_8_out);
  or or_1 (or_1_out, out_17, out_15);
  or or_2 (or_2_out, out_18, and_6_out, and_3_out);
  xor xor_1 (xor_1_out, and_2_out, and_1_out);
  and and_3 (and_3_out, and_1_out, comparator_1_gt);
  Comparator #(.width(4), .mode("unsigned")) comparator_1 (
    .a(SLOT_B), .b(SLOT_A), .gt(comparator_1_gt), .eq(comparator_1_eq), .lt(comparator_1_lt));
  and and_4 (out_15, comparator_1_lt, and_2_out);
  and and_5 (out_18, and_1_out, xor_1_out);
  not not_1 (not_1_out, and_1_out);
  and and_6 (and_6_out, comparator_1_eq, and_1_out);
  and and_7 (out_17, xor_1_out, not_1_out);
  or or_3 (out_16, and_3_out, and_6_out);

  // Notes on the sheet:
  //                                 Enter Password A
  //   Slot B is leading in tender
  //   Slot A is leading in tender
  //   Enter Password B
  //   Slot B is leading and 
  //   Slot A lost due to unautheticity
  //   Slot A is leading and 
  //   Slot B lost due to unautheticity
endmodule
